// Logisim project Groupe 13 - Romain KAUFFMANN Killian HIRTZLIN Thibault SABLONE Antoine MOHR - Schéma logique 3 capteurs.circ as structural Verilog: 1 circuit, main circuit main
// Moteurs gauches
module main (
  input  Capteur_ligne_n_1_gauche,
  input  Capteur_ligne_n_2_milieu,
  input  Capteur_ligne_n_3_droite,
  output Moteurs_gauche,
  output Moteurs_droite
);

  wire and_1_out, and_2_out, not_1_out, not_2_out;

  not not_1 (not_1_out, Capteur_ligne_n_1_gauche);
  and and_1 (and_1_out, Capteur_ligne_n_3_droite, Capteur_ligne_n_2_milieu);
  or or_1 (Moteurs_gauche, and_1_out, not_1_out);
  not not_2 (not_2_out, Capteur_ligne_n_3_droite);
  or or_2 (Moteurs_droite, not_2_out, and_2_out);
  and and_2 (and_2_out, Capteur_ligne_n_2_milieu, Capteur_ligne_n_1_gauche);

  // Notes on the sheet:
  //   Groupe 13
  //   Cas de 3 capteurs
endmodule
