// Logisim project Groupe 13 - Romain KAUFFMANN Killian HIRTZLIN Thibault SABLONE Antoine MOHR - Schéma logique 4 capteurs.circ as structural Verilog: 1 circuit, main circuit Capteur ligne n°1 (gauche du vehicule)
module Capteur_ligne_n_1__gauche_du_vehicule (
  input  Capteur_ligne_n_1__gauche_du_vehicule,
  input  Capteur_ligne_n_2__milieu_gauche_du_vehicule,
  input  Capteur_ligne_n_3__milieu_droite_du_vehicule,
  input  Capteur_ligne_n_4__droite_du_vehicule,
  output Moteurs_Droite,
  output Moteurs_Gauche
);

  wire and_1_out, and_2_out, and_3_out, and_4_out, and_5_out, and_6_out, not_1_out, not_2_out, not_3_out,
       not_4_out, not_5_out, not_6_out, not_7_out;

  not not_1 (not_1_out, Capteur_ligne_n_4__droite_du_vehicule);
  and and_1 (and_1_out, not_1_out, not_2_out);
  not not_2 (not_2_out, Capteur_ligne_n_3__milieu_droite_du_vehicule);
  and and_2 (and_2_out, not_1_out, Capteur_ligne_n_2__milieu_gauche_du_vehicule);
  or or_1 (Moteurs_Droite, and_1_out, and_2_out, and_3_out);
  not not_3 (not_3_out, Capteur_ligne_n_2__milieu_gauche_du_vehicule);
  and and_3 (and_3_out, not_1_out, not_3_out, not_4_out);
  not not_4 (not_4_out, Capteur_ligne_n_1__gauche_du_vehicule);
  not not_5 (not_5_out, Capteur_ligne_n_4__droite_du_vehicule);
  and and_4 (and_4_out, not_5_out, Capteur_ligne_n_2__milieu_gauche_du_vehicule, not_7_out);
  and and_5 (and_5_out, Capteur_ligne_n_4__droite_du_vehicule, Capteur_ligne_n_2__milieu_gauche_du_vehicule, Capteur_ligne_n_3__milieu_droite_du_vehicule);
  not not_6 (not_6_out, Capteur_ligne_n_2__milieu_gauche_du_vehicule);
  or or_2 (Moteurs_Gauche, and_4_out, and_5_out, and_6_out);
  and and_6 (and_6_out, not_6_out, not_7_out);
  not not_7 (not_7_out, Capteur_ligne_n_1__gauche_du_vehicule);

  // Notes on the sheet:
  //   Groupe 13
  //   Cas de 4 capteurs
  //   NB : Gère les intersections en allant vers la gauche tout le temps
  //   Schéma moins etoffé que l'autre, car nous avons choisi d'utiliser le modèle 3 capteurs
endmodule
